# Fritzing sketch PID_Rough_Draft (saved by Fritzing 0.9.3b)
breadboards: 4

parts:
  Part1 = Arduino Uno (Rev3)
  Q1 = PHOTOTRANSISTOR REFLECTIVE OBJECT SENSOR [package=qrb1114-side]
  Q2 = NPN-Transistor [package="SOT-23 [SMD]"]
  R2 = Resistor [tolerance=±5% resistance=220 package=THT]
  M2 = DC Motor  # not connected
  R3 = Rotary Potentiometer (Small) [maximum_resistance=100kΩ package=THT]
  Part2 = Arduino Uno (Rev3)
  VCC3 = Battery  # not connected
  VCC5 = Battery  # not connected
  START_2 = Toggle Switch [package=THT]
  LED1 = LED - 5mm [color="Red (633nm)" package="5 mm [THT]"]  # not connected
  Adjust_Brightness_++_-- = Pushbutton [package="[THT]"]
  S3 = Pushbutton [package="[THT]"]
  LED2 = LED - 5mm [color="Red (633nm)" package="5 mm [THT]"]  # not connected
  SELECT_4 = Toggle Switch [package=THT]
  Q3 = NPN-Transistor [package="SOT-23 [SMD]"]  # not connected
  LCD2 = LCD screen
  LCM1602_IIC2 = LCM1602 IIC [part_number="LCM1602 IIC" chip_label="LCM1602 IIC" package="DIP (Dual Inline) [THT]"]
  R4 = Resistor [tolerance=±5% resistance=10k package=THT]
  R5 = Resistor [tolerance=±5% resistance=10k package=THT]
  R6 = Resistor [tolerance=±5% resistance=10k package=THT]
  R7 = Resistor [tolerance=±5% resistance=10k package=THT]

nets:
  N1: Part1.D8, Part1.D11_PWM/MOSI, Part1.D12/MISO, Part1.D7, R3.leg1, Part2.D8, Part2.D2, Part2.D4, Part2.D7, Part2.5V, START_2.L1, START_2.COM, Adjust_Brightness_++_--.Pin_3, Adjust_Brightness_++_--.Pin_4, S3.Pin_3, S3.Pin_4, SELECT_4.L1, SELECT_4.COM, R4.Pin_0, R5.Pin_0, R6.Pin_0, R7.Pin_0
  N2: Part1.GND, R4.Pin_1
  N3: Q1.A, Q1.K
  N4: Q1.E, Q2.1
  N5: Q2.0, R2.Pin_1
  N6: R3.wiper, Part2.A0
  N7: R3.leg2, Part2.GND
  N8: Adjust_Brightness_++_--.Pin_1, Adjust_Brightness_++_--.Pin_2
  N9: S3.Pin_1, S3.Pin_2
  VSS: LCD2.VSS, LCM1602_IIC2.VSS
  VDD: LCD2.VDD, LCM1602_IIC2.VDD
  N10: LCD2.V0, LCM1602_IIC2.V0
  N11: LCD2.RS, LCM1602_IIC2.RS
  N12: LCD2.R/W, LCM1602_IIC2.RW
  N13: LCD2.E, LCM1602_IIC2.E
  N14: LCD2.DB0, LCM1602_IIC2.D0
  N15: LCD2.DB1, LCM1602_IIC2.D1
  N16: LCD2.DB2, LCM1602_IIC2.D2
  N17: LCD2.DB3, LCM1602_IIC2.D3
  N18: LCD2.DB4, LCM1602_IIC2.D4
  N19: LCD2.DB5, LCM1602_IIC2.D5
  N20: LCD2.DB6, LCM1602_IIC2.D6
  N21: LCD2.DB7, LCM1602_IIC2.D7
  N22: LCD2.LED+, LCM1602_IIC2.A
  N23: LCD2.LED-, LCM1602_IIC2.K
  N24: LCM1602_IIC2.LED_A, LCM1602_IIC2.LED_B

custom parts:
  LCM1602 IIC: I2C-Module to use a 1602 or 2004 LCD on with the wire.h libory Serial LCD Modul
